# Fritzing sketch DiagramaEletrico (saved by Fritzing 0.9.9b)
breadboards: 1

parts:
  Mod1 = Raspberry Pi Pico
  WATER_PUMP1 = water pump/motor
  WATER_PUMP2 = water pump/motor
  WATER_PUMP3 = water pump/motor
  S1 = Pushbutton [package="[THT]"]
  S2 = Pushbutton [package="[THT]"]
  S3 = Pushbutton [package="[THT]"]
  Componente1 = FC-28 Soil Hygrometer Module - Probe
  Componente2 = FC-28 Soil Hygrometer Module
  Componente3 = FC-28 Soil Hygrometer Module
  Componente4 = FC-28 Soil Hygrometer Module
  M3 = 1 chan 5v relay module
  M4 = 1 chan 5v relay module
  M5 = 1 chan 5v relay module
  Componente5 = FC-28 Soil Hygrometer Module - Probe
  Componente6 = FC-28 Soil Hygrometer Module - Probe
  VCC1 = Battery block 9V

nets:
  GND: Mod1.pin_3, Mod1.pin_8, Mod1.pin_13, Mod1.pin_18, Mod1.pin_23, Mod1.pin_28, Mod1.pin_33, Mod1.pin_38, Mod1.pin_42, Componente2.GND, Componente3.GND, Componente4.GND, M3.pin_2, M4.pin_2, M5.pin_2
  N1: Mod1.pin_14, M5.pin_3
  N2: Mod1.pin_15, M4.pin_3
  N3: Mod1.pin_16, M3.pin_3
  N4: Mod1.pin_17, S3.Pin_1, S3.Pin_2
  N5: Mod1.pin_19, S2.Pin_1, S2.Pin_2
  N6: Mod1.pin_20, S1.Pin_1, S1.Pin_2
  N7: Mod1.pin_31, Componente4.AO
  N8: Mod1.pin_32, Componente3.AO
  N9: Mod1.pin_34, Componente2.AO
  VCC: Mod1.pin_36, S1.Pin_3, S1.Pin_4, S2.Pin_3, S2.Pin_4, S3.Pin_3, S3.Pin_4, Componente2.VCC, Componente3.VCC, Componente4.VCC, M3.pin_1, M4.pin_1, M5.pin_1
  N10: WATER_PUMP1.pin_1, M3.pin_4
  N11: WATER_PUMP1.pin_2, WATER_PUMP2.pin_2, WATER_PUMP3.pin_2, VCC1.+
  N12: WATER_PUMP2.pin_1, M4.pin_4
  N13: WATER_PUMP3.pin_1, M5.pin_4
  N14: Componente1.POS, Componente4.POS
  N15: Componente1.NEG, Componente4.NEG
  N16: Componente2.POS, Componente6.POS
  N17: Componente2.NEG, Componente6.NEG
  N18: Componente3.POS, Componente5.POS
  N19: Componente3.NEG, Componente5.NEG
  N20: M3.pin_5, M4.pin_5, M5.pin_5, VCC1.-

custom parts:
  Raspberry Pi Pico: Raspberry Pi Pico. Based around the RP2040 microcontroller the Pico is a low cost microcontroller device bringing Raspberry Pi quality, cost, and easy of use to the microcontroller space. Jan 2021, Split part in to two versions: SMD (this one) and tht. This one is single sided and uses the castellation pads to solder the module to the board (no holes, other than for the USB connector!). The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
  water pump/motor: WATER PUMP BY ARDUBLOCKTR
  FC-28 Soil Hygrometer Module - Probe: The FC-28 is a soil hygrometer module that uses the Texas Instruments LM393 comparator chip to provide an analog measurement of soil humidity.
  FC-28 Soil Hygrometer Module: The FC-28 is a soil hygrometer module that uses the Texas Instruments LM393 comparator chip to provide an analog measurement of soil humidity. The digital output is high when soil moisture is over a certain threshold, as determined by adjusting the potentiometer.
  1 chan 5v relay module: 1 Channel 5V Relay Module Board Shield with Optocoupler Support High and Low Level Trigger for Arduino.
